// Logisim project 8bit-computer.circ as structural Verilog: 3 circuits, main circuit main
module main (
  input  flag_reset
);

  wire adder_1_cout, and_1_out, clock_1_out, d_ff_1_q, isallzero_1_out_2, nor_1_out, not_1_out, not_2_out,
       or_1_out;
  wire [3:0] Instruction_Register_q, Program_Counter_q, register_1_q;
  wire [7:0] adder_1_out, negator_1_output, ram_1_data, register_2_q, Register_A_q, Register_B_q;
  wire [8:0] zero_q;
  wire [16:0] rom_1_data;
  wire [23:0] rom_2_data;

  not not_1 (not_1_out, rom_1_data[16]);
  not not_2 (not_2_out, and_1_out);
  Clock clock_1 (.out(clock_1_out));
  D_Flip_Flop #(.trigger("high")) d_ff_1 (
    .clk(1'b1), .D(not_1_out), .Q(d_ff_1_q), .en(1'b1), .reset(flag_reset));  // open: Qn, preset
  and and_1 (and_1_out, clock_1_out, d_ff_1_q);
  Register #(.width(4)) register_1 (
    .D(ram_1_data[3:0]), .en(rom_1_data[15]), .Q(register_1_q), .clk(and_1_out), .clr(flag_reset));
  Register Instruction_Register (
    .D(ram_1_data), .en(rom_1_data[12]), .Q({zero_q[8:5], Instruction_Register_q}), .clk(and_1_out),
    .clr(flag_reset));
  Counter #(.width(3), .max('h7)) counter_1 (
    .count(1'b1), .Q(zero_q[4:2]), .clk(not_2_out), .clr(or_1_out));  // open: load, D, carry
  or or_1 (or_1_out, flag_reset, isallzero_1_out_2);
  RAM #(.addrWidth(4), .bus("separate")) ram_1 (
    .addr(register_1_q), .din(ram_1_data), .data(ram_1_data), .str(rom_1_data[13]), .clk(and_1_out),
    .ld(rom_1_data[14]));  // open: sel, clr
  ROM #(.addrWidth(9), .dataWidth(17)) rom_1 (.addr(zero_q), .data(rom_1_data));  // open: sel
  Pull_Resistor pull_resistor_1 (.node(and_1_out));
  assign ram_1_data[3:0] = rom_1_data[11] ? Instruction_Register_q : 4'bz;  // Controlled_Buffer controlled_buffer_1
  isAllZero isallzero_1 (.\input (rom_1_data), .out_2(isallzero_1_out_2));
  Pull_Resistor pull_resistor_2 (.node(ram_1_data[5]));
  Pull_Resistor pull_resistor_3 (.node(ram_1_data[7]));
  Pull_Resistor pull_resistor_4 (.node(ram_1_data[6]));
  Pull_Resistor pull_resistor_5 (.node(ram_1_data[4]));
  Pull_Resistor pull_resistor_6 (.node(ram_1_data[2]));
  Pull_Resistor pull_resistor_7 (.node(ram_1_data[0]));
  Pull_Resistor pull_resistor_8 (.node(ram_1_data[1]));
  Pull_Resistor pull_resistor_9 (.node(ram_1_data[3]));
  Counter #(.width(4), .max('hf)) Program_Counter (
    .load(rom_1_data[8]), .D(ram_1_data[3:0]), .count(rom_1_data[10]), .Q(Program_Counter_q),
    .clk(and_1_out), .clr(flag_reset));  // open: carry
  Negator negator_1 (.Input(Register_B_q), .Negate_signal__1___negate(rom_1_data[1]), .Output(negator_1_output));
  assign ram_1_data[3:0] = rom_1_data[9] ? Program_Counter_q : 4'bz;  // Controlled_Buffer controlled_buffer_2
  Register Register_A (.D(ram_1_data), .en(rom_1_data[7]), .Q(Register_A_q), .clk(and_1_out), .clr(flag_reset));
  assign ram_1_data = rom_1_data[6] ? Register_A_q : 8'bz;  // Controlled_Buffer controlled_buffer_3
  Adder adder_1 (.a(Register_A_q), .b(negator_1_output), .out(adder_1_out), .cout(adder_1_cout));  // open: cin
  assign ram_1_data = rom_1_data[5] ? adder_1_out : 8'bz;  // Controlled_Buffer controlled_buffer_4
  Register Register_B (.D(ram_1_data), .en(rom_1_data[4]), .Q(Register_B_q), .clk(and_1_out), .clr(flag_reset));
  assign ram_1_data = rom_1_data[3] ? Register_B_q : 8'bz;  // Controlled_Buffer controlled_buffer_5
  Register register_2 (.D(ram_1_data), .en(rom_1_data[2]), .Q(register_2_q), .clk(and_1_out), .clr(flag_reset));
  Register #(.width(1)) carry (.D(adder_1_cout), .en(rom_1_data[0]), .Q(zero_q[1]), .clk(and_1_out), .clr(flag_reset));
  Register #(.width(1)) zero (.D(nor_1_out), .en(rom_1_data[0]), .Q(zero_q[0]), .clk(and_1_out), .clr(flag_reset));
  ROM #(.dataWidth(24)) rom_2 (.addr(register_2_q), .data(rom_2_data));  // open: sel
  nor nor_1 (nor_1_out, adder_1_out[0], adder_1_out[1], adder_1_out[2], adder_1_out[3], adder_1_out[4], adder_1_out[5], adder_1_out[6], adder_1_out[7]);
  _7_Segment_Display u_7_segment_display_1 (
    .g(rom_2_data[14]), .f(rom_2_data[15]), .a(rom_2_data[20]), .b(rom_2_data[19]), .e(rom_2_data[16]),
    .d(rom_2_data[17]), .c(rom_2_data[18]));  // open: dp
  _7_Segment_Display u_7_segment_display_2 (
    .g(rom_2_data[7]), .f(rom_2_data[8]), .a(rom_2_data[13]), .b(rom_2_data[12]), .e(rom_2_data[9]),
    .d(rom_2_data[10]), .c(rom_2_data[11]));  // open: dp
  _7_Segment_Display u_7_segment_display_3 (
    .g(rom_2_data[0]), .f(rom_2_data[1]), .a(rom_2_data[6]), .b(rom_2_data[5]), .e(rom_2_data[2]),
    .d(rom_2_data[3]), .c(rom_2_data[4]));  // open: dp

  // Notes on the sheet:
  //   opcode counter reset
  //   clock halt reset
  //   MI
  //   H
  //   MR
  //   IR
  //   CR
  //   AR
  //   BR
  //   OR
  //   RESET
  //   inverted clock line
  //   RI
  //   II
  //   RO
  //   CO
  //   CE
  //   IO
  //   contents of rom_1 (hex, n*v repeats v):
  //   4*8200 4*5400 4*8800 4*4080 16*0 4*8200 4*5400 4*8800 4*4010 4*a1 12*0 4*8200 4*5400 4*44 52*0
  //   4*8200 4*5400 4*900 20*0 4*8200 4*5400 0 0 900 900 20*0 4*8200 4*5400 0 900 0 900 20*0 4*8200 4*5400
  //   4*8800 4*4010 4*a3 12*0 4*8200 4*5400 4*880 20*0 4*8200 4*5400 4*8800 4*2040 176*0 4*8200 4*5400
  //   4*10000
  //   J
  //   AI
  //   AO
  //   SO
  //   BI
  //   BO
  //   reset counter if no instruction
  //   OI
  //   SU
  //   FI
  //   Flag registers
  //   contents of rom_2 (hex, n*v repeats v):
  //   1fbf7e 1fbf30 1fbf6d 1fbf79 1fbf33 1fbf5b 1fbf5f 1fbf70 1fbf7f 1fbf7b 1f987e 1f9830 1f986d 1f9879
  //   1f9833 1f985b 1f985f 1f9870 1f987f 1f987b 1fb6fe 1fb6b0 1fb6ed 1fb6f9 1fb6b3 1fb6db 1fb6df 1fb6f0
  //   1fb6ff 1fb6fb 1fbcfe 1fbcb0 1fbced 1fbcf9 1fbcb3 1fbcdb 1fbcdf 1fbcf0 1fbcff 1fbcfb 1f99fe 1f99b0
  //   1f99ed 1f99f9 1f99b3 1f99db 1f99df 1f99f0 1f99ff 1f99fb 1fadfe 1fadb0 1faded 1fadf9 1fadb3 1faddb
  //   1faddf 1fadf0 1fadff 1fadfb 1faffe 1fafb0 1fafed 1faff9 1fafb3 1fafdb 1fafdf 1faff0 1fafff 1faffb
  //   1fb87e 1fb830 1fb86d 1fb879 1fb833 1fb85b 1fb85f 1fb870 1fb87f 1fb87b 1fbffe 1fbfb0 1fbfed 1fbff9
  //   1fbfb3 1fbfdb 1fbfdf 1fbff0 1fbfff 1fbffb 1fbdfe 1fbdb0 1fbded 1fbdf9 1fbdb3 1fbddb 1fbddf 1fbdf0
  //   1fbdff 1fbdfb c3f7e c3f30 c3f6d c3f79 c3f33 c3f5b c3f5f c3f70 c3f7f c3f7b c187e c1830 c186d c1879
  //   c1833 c185b c185f c1870 c187f c187b c36fe c36b0 c36ed c36f9 c36b3 c36db c36df c36f0 c36ff c36fb
  //   c3cfe c3cb0 c3ced c3cf9 c3cb3 c3cdb c3cdf c3cf0 c3cff c3cfb c19fe c19b0 c19ed c19f9 c19b3 c19db
  //   c19df c19f0 c19ff c19fb c2dfe c2db0 c2ded c2df9 c2db3 c2ddb c2ddf c2df0 c2dff c2dfb c2ffe c2fb0
  //   c2fed c2ff9 c2fb3 c2fdb c2fdf c2ff0 c2fff c2ffb c387e c3830 c386d c3879 c3833 c385b c385f c3870
  //   c387f c387b c3ffe c3fb0 c3fed c3ff9 c3fb3 c3fdb c3fdf c3ff0 c3fff c3ffb c3dfe c3db0 c3ded c3df9
  //   c3db3 c3ddb c3ddf c3df0 c3dff c3dfb 1b7f7e 1b7f30 1b7f6d 1b7f79 1b7f33 1b7f5b 1b7f5f 1b7f70 1b7f7f
  //   1b7f7b 1b587e 1b5830 1b586d 1b5879 1b5833 1b585b 1b585f 1b5870 1b587f 1b587b 1b76fe 1b76b0 1b76ed
  //   1b76f9 1b76b3 1b76db 1b76df 1b76f0 1b76ff 1b76fb 1b7cfe 1b7cb0 1b7ced 1b7cf9 1b7cb3 1b7cdb 1b7cdf
  //   1b7cf0 1b7cff 1b7cfb 1b59fe 1b59b0 1b59ed 1b59f9 1b59b3 1b59db 1b59df 1b59f0 1b59ff 1b59fb 1b6dfe
  //   1b6db0 1b6ded 1b6df9 1b6db3 1b6ddb
endmodule

module Negator (
  input  [7:0] Input,
  input  Negate_signal__1___negate,
  output [7:0] Output
);

  wire not_1_out;
  wire [7:0] negator_1_out;

  not not_1 (not_1_out, Negate_signal__1___negate);
  Negator_part negator_1 (.in(Input), .out(negator_1_out));
  BitSelector #(.width(16), .group(8)) bitselector_1 (.in({Input, negator_1_out}), .out(Output), .sel(not_1_out));
endmodule

module isAllZero (
  input  [16:0] \input ,
  output out_2
);

  nor nor_1 (out_2, \input [0], \input [1], \input [2], \input [3], \input [4], \input [5], \input [6], \input [7], \input [8], \input [9], \input [10], \input [11], \input [12], \input [13], \input [14], \input [15], \input [16]);
endmodule
